# Fritzing sketch Objenious_Push_button (saved by Fritzing 0.9.3b)

parts:
  Composant1 = The AirBoard
  S1 = Round Pushbutton

nets:
  N1: Composant1.D3~/INT1, S1.leg0
  N2: Composant1.3V3, S1.leg1

custom parts:
  The AirBoard: The AirBoard is an ultra low-power Arduino-compatible prototyping platform for the Internet of Things, designed to explore, hack and deploy your killer idea in the field. It features a Bee socket for Bluetooth, WiFi, XBee, GSM/GPRS, SIGFOX and LoRa wireless modules, with Over-The-Air Programming support for Bluetooth and XBee. It comes with a 155mAh built-in rechargeable LiPo battery with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
