# Fritzing sketch Objenious_Temperature (saved by Fritzing 0.9.3b)

parts:
  Composant1 = The AirBoard
  R1 = Temperature Sensor (Thermistor) [thermistor_type=NTC package=THT]
  R2 = Resistor [tolerance=±5% resistance=10k package=THT]

nets:
  N1: Composant1.D19/A5/SCL, R1.pin_0, R2.Pin_0
  N2: Composant1.3V3, R1.pin_1
  N3: Composant1.GND, R2.Pin_1

custom parts:
  The AirBoard: The AirBoard is an ultra low-power Arduino-compatible prototyping platform for the Internet of Things, designed to explore, hack and deploy your killer idea in the field. It features a Bee socket for Bluetooth, WiFi, XBee, GSM/GPRS, SIGFOX and LoRa wireless modules, with Over-The-Air Programming support for Bluetooth and XBee. It comes with a 155mAh built-in rechargeable LiPo battery with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
